# Fritzing sketch porte_poulailler_v2 (saved by Fritzing 0.9.3b)

parts:
  Composant1 = Arduino Nano (Rev3.0)
  ZS-042_RTC1 = ZS-042 RTC Module
  S1 = H-Bridge with L298N
  M1 = DC Motor
  Power_plug1 = Power plug
  S2 = Pushbutton [package="[THT]"]
  S4 = Toggle Switch [package=THT]
  S3 = Pushbutton [package="[THT]"]

nets:
  N1: Composant1.D4, S2.Pin_2
  N2: Composant1.D5, S3.Pin_2
  N3: Composant1.D6, S4.L1
  N4: Composant1.D8, S1.IN2
  N5: Composant1.D9, S1.IN1
  N6: Composant1.D10, S1.ENA
  N7: Composant1.A5, ZS-042_RTC1.SCL
  N8: Composant1.A4, ZS-042_RTC1.SDA
  VCC: ZS-042_RTC1.VCC, S1.5V
  12V: S1.12V, Power_plug1.VCC
  GND: S1.GND, Power_plug1.GND, S4.COM
  N9: S1.M1-01, M1.pin_2
  N10: S1.M1-02, M1.pin_1

notes:
  Boutons poussoirs
  Vert pour l'ouverture
  Jaune pour la fermeture
  capteur fin de course porte fermee
  rtc
  alim 12V
  moteur

custom parts:
  H-Bridge with L298N: h-bridge
